// Logisim project algebraic_pipeline.circ as structural Verilog: 1 circuit, main circuit main
module main (
  output [7:0] out_1,
  output [7:0] out_2,
  output [7:0] out_3,
  output [7:0] out_4,
  output [7:0] C,
  output [7:0] E,
  output [7:0] F,
  output [7:0] G,
  output [7:0] out_9,
  output [7:0] out_10
);

  wire clock_1_out, clock_2_out;
  wire [7:0] adder_1_out, adder_2_out, adder_3_out, counter_1_q, counter_2_q, counter_3_q, counter_4_q,
       divider_1_out, multiplier_1_out, multiplier_2_out, register_2_q, register_3_q, register_4_q,
       register_5_q, register_6_q, register_7_q, register_8_q, register_9_q, register_10_q, register_12_q,
       register_13_q, register_15_q, register_16_q, register_17_q, register_18_q, subtractor_1_out;

  Clock clock_1 (.out(clock_1_out));
  Counter counter_1 (.Q(counter_1_q), .clk(clock_1_out));  // open: load, D, count, carry, clr
  Register register_1 (.D(out_1), .Q(C), .clk(clock_2_out));  // open: en, clr
  ROM rom_1 (.addr(counter_1_q), .data(out_1));  // open: sel
  Register register_2 (.D(out_1), .Q(register_2_q), .clk(clock_2_out));  // open: en, clr
  Adder adder_1 (.a(register_2_q), .b(register_4_q), .out(adder_1_out));  // open: cin, cout
  Register register_3 (.D(adder_1_out), .Q(register_3_q), .clk(clock_2_out));  // open: en, clr
  Counter counter_2 (.Q(counter_2_q), .clk(clock_1_out));  // open: load, D, count, carry, clr
  Register register_4 (.D(out_2), .Q(register_4_q), .clk(clock_2_out));  // open: en, clr
  Multiplier multiplier_1 (.a(register_3_q), .b(register_7_q), .out(multiplier_1_out));  // open: cin, cout
  Register register_5 (.D(multiplier_1_out), .Q(register_5_q), .clk(clock_2_out));  // open: en, clr
  Register register_6 (.D(out_3), .Q(register_6_q), .clk(clock_2_out));  // open: en, clr
  Register register_7 (.D(C), .Q(register_7_q), .clk(clock_2_out));  // open: en, clr
  Subtractor subtractor_1 (.a(register_5_q), .b(register_12_q), .out(subtractor_1_out));  // open: bin, bout
  ROM rom_2 (.addr(counter_2_q), .data(out_2));  // open: sel
  Counter counter_3 (.Q(counter_3_q), .clk(clock_1_out));  // open: load, D, count, carry, clr
  Register register_8 (.D(out_4), .Q(register_8_q), .clk(clock_2_out));  // open: en, clr
  Divider divider_1 (.a(register_6_q), .b(register_8_q), .out(divider_1_out), .rem(out_9));  // open: upper
  Register register_9 (.D(divider_1_out), .Q(register_9_q), .clk(clock_2_out));  // open: en, clr
  Register register_10 (.D(subtractor_1_out), .Q(register_10_q), .clk(clock_2_out));  // open: en, clr
  Register register_11 (.D(out_2), .Q(E), .clk(clock_2_out));  // open: en, clr
  Adder adder_2 (.a(register_9_q), .b(register_13_q), .out(adder_2_out));  // open: cin, cout
  Register register_12 (.D(adder_2_out), .Q(register_12_q), .clk(clock_2_out));  // open: en, clr
  Adder adder_3 (.a(register_10_q), .b(register_16_q), .out(adder_3_out));  // open: cin, cout
  ROM rom_3 (.addr(counter_3_q), .data(out_3));  // open: sel
  Register register_13 (.D(E), .Q(register_13_q), .clk(clock_2_out));  // open: en, clr
  Register register_14 (.D(adder_3_out), .Q(out_10), .clk(clock_2_out));  // open: en, clr
  Counter counter_4 (.Q(counter_4_q), .clk(clock_1_out));  // open: load, D, count, carry, clr
  Register register_15 (.D(F), .Q(register_15_q), .clk(clock_2_out));  // open: en, clr
  Multiplier multiplier_2 (.a(register_15_q), .b(register_17_q), .out(multiplier_2_out));  // open: cin, cout
  Register register_16 (.D(register_18_q), .Q(register_16_q), .clk(clock_2_out));  // open: en, clr
  ROM rom_4 (.addr(counter_4_q), .data(out_4));  // open: sel
  Register register_17 (.D(G), .Q(register_17_q), .clk(clock_2_out));  // open: en, clr
  Register register_18 (.D(multiplier_2_out), .Q(register_18_q), .clk(clock_2_out));  // open: en, clr
  Register register_19 (.D(out_3), .Q(F), .clk(clock_2_out));  // open: en, clr
  Register register_20 (.D(out_4), .Q(G), .clk(clock_2_out), .clr(clock_2_out));  // open: en
  Clock clock_2 (.out(clock_2_out));

  // Notes on the sheet:
  //   A
  //   contents of rom_1 (hex, n*v repeats v):
  //   0 8 5 9 8 6 3 8 5 6 7 5 7 6 8 6 5 2 3 9 8 7 6 9 1 2 3 4 5 6 7 8 9 6 3 7 1 2 3 7 3 6 4 5 2 3 3 3 6 8
  //   3 1 7 3 6 1 3 8 9 1 2 4 5 9 6 7 7 6 8 6 2 13 12 18 1 1 2 1 2 3 9 6 3 4 7 5 6 3 7 8 6 7 5 3 7 6
  //   D
  //   B
  //   (A+D)*C
  //   (A+D)*C-(B/H+E)
  //   EQUATION  Fn = ( A + D ) * C - ( B / H + E ) + F * G
  //   contents of rom_2 (hex, n*v repeats v):
  //   0 6 5 4 12 7 10 9 12 11 3 6 7 6 9 6 9 2 3 9 8 7 6 9 1 2 3 4 5 6 7 8 6 5 5 8 9 8 7 6 5 4 3 2 1 1 2 3
  //   4 5 6 7 8 9 10 11 12 11 10 9 8 7 6 5 4 3 2 1 11 9 4 5 3 7 6 3 11 10 9 8 7 5 6 3 2 1 3 3 7 6 4 2 3 2
  //   6 8 7 5 3 2 4 5 6 9 4 5 2 1 6 7 8 5
  //   H
  //   B/H+E
  //   contents of rom_3 (hex, n*v repeats v):
  //   cf b 5 47 86 96 41 65 25 69 74 6 7 6 88 6 41 2 3 9 8 7 6 9 1 2 3 4 5 6 7 8
  //   (A+D)*C-(B/H+E)+F*G
  //   contents of rom_4 (hex, n*v repeats v):
  //   9 8 7 6 2 6 7 3 2 3 6 8 7 6 2 6 8 2 3 9 8 7 6 9 1 2 3 4 5 6 7 8 3 6 6 3 7 8 9 10 1 5 6 7 8 6 3 3 4 2
  //   3 6 8 6 3 3 8 5 6 7 1 5 6 6 6 7 2 3 9 6 3 4 6 8 9 7 5 6 1 3 9 4 9 4 9 4 6 1 3 2 4 6 5 9 8 1
  //   F*G
  //   Fn
endmodule
